// Logisim project y86.circ as structural Verilog: 19 circuits, main circuit main
module main (
  input  in_1,
  input  Reset
);

  wire and_1_out, Clock_out, Cnd, dmemerr, imem_1_p4, imem_1_p5, imem_1_p6, imem_1_p7, imem_1_p8, imem_1_p9,
       imem_1_p10, imem_1_p11, imem_1_p12, imemerr, instrvalid, needregs, needvalc, nor_1_out, not_1_out,
       read_write_1_read, read_write_1_write, regfile_1_p7, setcc_1_out_2;
  wire [1:0] stat_1_out_5, Stat_2_q;
  wire [2:0] CC_q, undriven;
  wire [3:0] alu_fun_1_alu_fun, dstE, dstM, icode, ifun, rA, rB, srcA, srcB;
  wire [7:0] imem_1_p3;
  wire [31:0] Addr_0, addressdata_1_addr_1, addressdata_1_mem_0, align_1_p13, aluA_0, alua_1_bit_1, aluB_0,
       alub_1_bit_1, Data_0, newPC, newpc_1_out_6, PC_q, regfile_1_p4, regfile_1_p11, regfile_1_p13, valA_0,
       valB_0, valC_0, valE_0, valM_0, valP;

  and and_1 (and_1_out, Clock_out, nor_1_out);
  Clock Clock (.out(Clock_out));
  nor nor_1 (nor_1_out, Stat_2_q[1], Stat_2_q[0]);
  PCincrement pcincrement_1 (.valP(valP), .pcin_32(PC_q), .needvalC(needvalc), .needReg(needregs));
  Register #(.width(32)) PC (.D(newPC), .Q(PC_q), .clk(and_1_out), .clr(Reset));  // open: en
  not not_1 (not_1_out, and_1_out);
  Split split_1 (.imemerr(imemerr), .valid(instrvalid), .ifun(ifun), .B0(imem_1_p3), .icode(icode));
  // imem imem_1: pin names not known; wires that end beside it: PC_q, imemerr, imem_1_p3, imem_1_p4, imem_1_p5, imem_1_p6, imem_1_p7, imem_1_p8, imem_1_p9, imem_1_p10, imem_1_p11, imem_1_p12, imem_1_p4
  stat stat_1 (.out_5(stat_1_out_5), .icode(icode), .instr_valid(instrvalid), .imem_err(imemerr), .dmem_err(dmemerr));
  // Probe on stat_1_out_5
  needvalC needvalc_1 (.needvalc(needvalc), .icode(icode));
  needreg needreg_1 (.icode(icode), .needreg(needregs));
  // y86__old__Align align_1: pin names not known; wires that end beside it: imem_1_p5, imem_1_p6, imem_1_p7, imem_1_p8, imem_1_p9, imem_1_p10, imem_1_p11, imem_1_p12, needregs, rA, rB, valC_0, align_1_p13
  Register #(.width(2)) Stat_2 (.D(stat_1_out_5), .Q(Stat_2_q), .clk(not_1_out), .clr(Reset));  // open: en
  srcAB srcab_1 (.srcA(srcA), .rA(rA), .icode(icode), .srrcB(srcB), .rB(rB));
  dstM dstm_1 (.dstM(dstM), .icode(icode), .rA(rA));
  dstE dste_1 (.dstE(dstE), .icode(icode), .rB(rB), .Cnd(Cnd));
  // Probe on icode
  // Probe on srcA
  // Probe on dstM
  // regfile regfile_1: pin names not known; wires that end beside it: srcA, srcB, dstE, regfile_1_p4, valE_0, dstM, regfile_1_p7, valM_0, not_1_out, Reset, regfile_1_p11, valA_0, regfile_1_p13, valB_0
  // Probe on ifun
  // Probe on rA
  // Probe on srcB
  // Probe on dstE
  aluA alua_1 (
    .bit_1(alua_1_bit_1), .bit_0(aluA_0), .valA_1(regfile_1_p11), .valA_0(valA_0), .valC_1(align_1_p13),
    .valC_0(valC_0), .icode(icode));
  aluB alub_1 (.bit_1(alub_1_bit_1), .bit_0(aluB_0), .icode(icode), .valB_1(regfile_1_p13), .valB_0(valB_0));
  // Probe on rB
  ALU_fun alu_fun_1 (.ALU_fun(alu_fun_1_alu_fun), .icode(icode), .ifun(ifun));
  // Probe on valC_0
  // Probe on valE_0
  setCC setcc_1 (.out_2(setcc_1_out_2), .icode(icode));
  Register #(.width(3)) CC (.D(undriven), .en(setcc_1_out_2), .Q(CC_q), .clk(not_1_out), .clr(Reset));
  // alu alu_1: pin names not known; wires that end beside it: alua_1_bit_1, aluA_0, alub_1_bit_1, aluB_0, alu_fun_1_alu_fun, regfile_1_p4, valE_0
  // Probe on valP
  // Probe on Addr_0
  Cond cond_1 (.out_3(Cnd), .ifun(ifun), .s(CC_q));
  // Probe on valA_0
  // Probe on Data_0
  addressData addressdata_1 (
    .Addr_1(addressdata_1_addr_1), .Addr_0(Addr_0), .icode(icode), .valE_1(regfile_1_p4), .valE_0(valE_0),
    .valA_1(regfile_1_p11), .valA_0(valA_0), .valP_1({32{1'b0}}), .Mem_1(Data_0),
    .Mem_0(addressdata_1_mem_0), .valP_0(valP));
  read_write read_write_1 (.read(read_write_1_read), .icode(icode), .write(read_write_1_write));
  // Probe on aluA_0
  // Probe on valM_0
  // dmem dmem_1: pin names not known; wires that end beside it: addressdata_1_addr_1, Addr_0, Data_0, addressdata_1_mem_0, read_write_1_read, read_write_1_write, dmemerr, not_1_out, in_1, regfile_1_p7, valM_0, regfile_1_p4, regfile_1_p11, align_1_p13
  // Probe on aluB_0
  newPC newpc_1 (.valP(valP), .valC_0(valC_0), .valM_0(valM_0), .out_6(newpc_1_out_6), .icode(icode), .Cnd(Cnd));
  Register #(.width(32)) PChold (.D(newpc_1_out_6), .Q(newPC), .clk(not_1_out), .clr(Reset));  // open: en
  // Probe on newpc_1_out_6

  // Notes on the sheet:
  //   y86 CPU by Gabriele Bieliauskaite, Chris Castillo, and Edric Choi 
endmodule

// A\nl\ni\ng\nn
module Align (
  input  [7:0] B1,
  input  [7:0] B2,
  input  [7:0] B3,
  input  [7:0] B4,
  input  [7:0] B5,
  input  [7:0] B6,
  input  [7:0] B7,
  input  [7:0] B8,
  input  [7:0] B9,
  input  NeedRegs,
  output [3:0] rA,
  output [3:0] rB,
  output [31:0] valC_0,
  output [31:0] valC_1
);

  wire undriven;

  // Probe on B1[3:0]
  // Probe on B1[7:4]
  Multiplexer #(.width(4)) multiplexer_1 (.in0(4'b0000), .in1(B1[7:4]), .out(rA), .sel(NeedRegs));  // open: en
  Multiplexer #(.width(4)) multiplexer_2 (.in0(4'b0000), .in1(B1[3:0]), .out(rB), .sel(NeedRegs), .en(undriven));
  Multiplexer #(.width(32)) multiplexer_3 (
    .in0({B4, B3, B2, B1}), .in1({B5, B4, B3, B2}), .out(valC_0), .sel(NeedRegs));  // open: en
  Multiplexer #(.width(32)) multiplexer_4 (
    .in0({B8, B7, B6, B5}), .in1({B9, B8, B7, B6}), .out(valC_1), .sel(NeedRegs));  // open: en
endmodule

// new\nPC
module newPC (
  input  [3:0] icode,
  input  Cnd,
  input  [31:0] valC_0,
  input  [31:0] valM_0,
  input  [31:0] valP,
  output [31:0] out_6
);

  wire and_2_out, and_3_out, and_4_out, and_5_out, and_6_out, CndEq, comparator_1_eq, not_1_out, not_2_out,
       not_3_out, not_4_out, not_5_out, not_6_out, not_7_out, not_8_out, not_9_out;
  wire [1:0] S;
  wire [31:0] multiplexer_1_out;

  Multiplexer #(.width(32), .enable("false")) multiplexer_1 (
    .in0(valP), .in1(valC_0), .out(multiplexer_1_out), .sel(CndEq));
  Multiplexer #(.select(2), .width(32), .enable("false")) multiplexer_2 (
    .in0(valC_0), .in1(multiplexer_1_out), .in2(valM_0), .in3(valP), .out(out_6), .sel(S));
  Comparator #(.width(4)) comparator_1 (.a(icode), .b(4'b0111), .eq(comparator_1_eq));  // open: gt, lt
  and and_1 (CndEq, Cnd, comparator_1_eq);
  not not_1 (not_1_out, icode[3]);
  not not_2 (not_2_out, icode[2]);
  not not_3 (not_3_out, icode[3]);
  not not_4 (not_4_out, icode[1]);
  not not_5 (not_5_out, icode[3]);
  not not_6 (not_6_out, icode[0]);
  not not_7 (not_7_out, icode[2]);
  not not_8 (not_8_out, icode[2]);
  not not_9 (not_9_out, icode[3]);
  and and_2 (and_2_out, not_1_out, not_2_out);
  and and_3 (and_3_out, not_3_out, not_4_out);
  and and_4 (and_4_out, not_5_out, not_6_out);
  and and_5 (and_5_out, not_7_out, icode[0]);
  and and_6 (and_6_out, not_8_out, icode[1]);
  or or_1 (S[0], not_9_out, icode[1]);
  or or_2 (S[1], and_2_out, and_3_out, and_4_out, and_5_out, and_6_out);

  // Other names for the same wires on the sheet: i0 = icode[0]; i1 = icode[1]; i2 = icode[2]; i3 = icode[3]
endmodule

// Add\nData
module addressData (
  input  [3:0] icode,
  input  [31:0] valE_1,
  input  [31:0] valE_0,
  input  [31:0] valA_1,
  input  [31:0] valA_0,
  input  [31:0] valP_1,
  input  [31:0] valP_0,
  output [31:0] Addr_1,
  output [31:0] Addr_0,
  output [31:0] Mem_1,
  output [31:0] Mem_0
);

  wire and_1_out, and_2_out, and_4_out, and_5_out, not_1_out, not_2_out, not_3_out, not_4_out, not_5_out,
       not_6_out, not_7_out, not_8_out, not_9_out;
  wire [1:0] S, S2;

  Multiplexer #(.select(2), .width(32), .enable("false")) multiplexer_1 (
    .in0(valE_1), .in1(valA_1), .in2({32{1'b1}}), .out(Addr_1), .sel(S));  // open: in3
  Multiplexer #(.select(2), .width(32), .enable("false")) multiplexer_2 (
    .in0(valE_0), .in1(valA_0), .in2({32{1'b1}}), .out(Addr_0), .sel(S));  // open: in3
  Multiplexer #(.select(2), .width(32), .enable("false")) multiplexer_3 (
    .in0(valA_1), .in1(valP_1), .in2({32{1'b1}}), .out(Mem_1), .sel(S2));  // open: in3
  Multiplexer #(.select(2), .width(32), .enable("false")) multiplexer_4 (
    .in0(valA_0), .in1(valP_0), .in2({32{1'b1}}), .out(Mem_0), .sel(S2));  // open: in3
  not not_1 (not_1_out, icode[3]);
  not not_2 (not_2_out, icode[2]);
  not not_3 (not_3_out, icode[3]);
  not not_4 (not_4_out, icode[2]);
  not not_5 (not_5_out, icode[3]);
  not not_6 (not_6_out, icode[2]);
  not not_7 (not_7_out, icode[3]);
  not not_8 (not_8_out, icode[2]);
  not not_9 (not_9_out, icode[1]);
  and and_1 (and_1_out, not_1_out, not_2_out);
  and and_2 (and_2_out, not_3_out, icode[1]);
  and and_3 (S[0], not_4_out, icode[0]);
  and and_4 (and_4_out, not_5_out, not_6_out);
  and and_5 (and_5_out, not_7_out, icode[1]);
  and and_6 (S2[0], not_8_out, not_9_out);
  or or_1 (S[1], and_1_out, and_2_out);
  or or_2 (S2[1], and_4_out, icode[0], and_5_out);

  // Other names for the same wires on the sheet: i0 = icode[0]; i1 = icode[1]; i2 = icode[2]; i3 = icode[3]
endmodule

// R/W
module read_write (
  input  [3:0] icode,
  output read,
  output write
);

  wire and_1_out, and_2_out, and_3_out, and_4_out, not_1_out, not_2_out, not_3_out, not_4_out;

  not not_1 (not_1_out, icode[1]);
  not not_2 (not_2_out, icode[1]);
  not not_3 (not_3_out, icode[0]);
  not not_4 (not_4_out, icode[0]);
  and and_1 (and_1_out, icode[2], not_1_out, icode[0]);
  and and_2 (and_2_out, icode[3], icode[0]);
  and and_3 (and_3_out, icode[2], not_2_out, not_3_out);
  and and_4 (and_4_out, icode[3], not_4_out);
  or or_1 (read, and_1_out, and_2_out);
  or or_2 (write, and_3_out, and_4_out);
endmodule

module aluA (
  input  [3:0] icode,
  input  [31:0] valA_1,
  input  [31:0] valA_0,
  input  [31:0] valC_1,
  input  [31:0] valC_0,
  output [31:0] bit_1,
  output [31:0] bit_0
);

  wire and_1_out, and_2_out, and_3_out, and_4_out, and_5_out, not_1_out, not_2_out, not_3_out, not_4_out,
       not_5_out, not_6_out, not_7_out;
  wire [2:0] or_2_out;
  wire [31:0] negator_1_out, negator_2_out;

  Negator #(.width(32)) negator_1 (.in(32'h1), .out(negator_1_out));
  Negator #(.width(32)) negator_2 (.in(32'h8), .out(negator_2_out));
  not not_1 (not_1_out, icode[3]);
  not not_2 (not_2_out, icode[2]);
  not not_3 (not_3_out, icode[1]);
  not not_4 (not_4_out, icode[3]);
  not not_5 (not_5_out, icode[1]);
  not not_6 (not_6_out, icode[3]);
  not not_7 (not_7_out, icode[0]);
  Multiplexer #(.select(3), .width(32), .enable("false")) multiplexer_1 (
    .in0(valA_1), .in1(valC_1), .in2({32{1'b0}}), .in3(negator_1_out), .in4(32'hf), .in5(32'hf), .in6(32'hf),
    .in7(32'hf), .out(bit_1), .sel({or_2_out[2], icode[3], or_2_out[0]}));
  Multiplexer #(.select(3), .width(32), .enable("false")) multiplexer_2 (
    .in0(valA_0), .in1(valC_0), .in2(32'h8), .in3(negator_2_out), .in4(32'hf), .in5(32'hf), .in6(32'hf),
    .in7(32'hf), .out(bit_0), .sel({or_2_out[2], icode[3], or_2_out[0]}));
  and and_1 (and_1_out, not_1_out, not_2_out, not_3_out);
  or or_1 (or_2_out[2], and_1_out, and_2_out);
  and and_2 (and_2_out, icode[2], icode[1], icode[0]);
  and and_3 (and_3_out, not_4_out, not_5_out);
  and and_4 (and_4_out, not_6_out, icode[0]);
  or or_2 (or_2_out[0], and_3_out, and_4_out, and_5_out);
  and and_5 (and_5_out, icode[3], not_7_out);
  // Probe on {or_2_out[2], icode[3], or_2_out[0]}
endmodule

module aluB (
  input  [3:0] icode,
  input  [31:0] valB_1,
  input  [31:0] valB_0,
  output [31:0] bit_1,
  output [31:0] bit_0
);

  wire and_1_out, and_2_out, not_1_out, not_2_out, not_3_out, not_4_out, not_5_out;
  wire [1:0] and_3_out;

  not not_1 (not_1_out, icode[3]);
  not not_2 (not_2_out, icode[2]);
  not not_3 (not_3_out, icode[1]);
  not not_4 (not_4_out, icode[3]);
  not not_5 (not_5_out, icode[2]);
  and and_1 (and_1_out, not_1_out, not_2_out, not_3_out);
  and and_2 (and_2_out, icode[2], icode[1], icode[0]);
  and and_3 (and_3_out[0], not_4_out, not_5_out);
  Multiplexer #(.select(2), .width(32), .enable("false")) multiplexer_1 (
    .in0(valB_1), .in1({32{1'b0}}), .in2(32'hf), .in3(32'hf), .out(bit_1), .sel(and_3_out));
  Multiplexer #(.select(2), .width(32), .enable("false")) multiplexer_2 (
    .in0(valB_0), .in1({32{1'b0}}), .in2(32'hf), .in3(32'hf), .out(bit_0), .sel(and_3_out));
  or or_1 (and_3_out[1], and_1_out, and_2_out);
endmodule

// ALU\nfun
module ALU_fun (
  input  [3:0] ifun,
  input  [3:0] icode,
  output [3:0] ALU_fun
);

  wire and_1_out, not_1_out;

  Multiplexer #(.width(4), .enable("false")) multiplexer_1 (.in0(4'b0000), .in1(ifun), .out(ALU_fun), .sel(and_1_out));
  and and_1 (and_1_out, icode[2], icode[1], not_1_out);
  not not_1 (not_1_out, icode[0]);
endmodule

module Cond (
  input  [2:0] s,
  input  [3:0] ifun,
  output out_3
);

  wire not_1_out, not_2_out, not_3_out, or_1_out, xor_1_out;

  xor xor_1 (xor_1_out, s[0], s[1]);
  or or_1 (or_1_out, xor_1_out, s[2]);
  not not_1 (not_1_out, xor_1_out);
  not not_2 (not_2_out, or_1_out);
  not not_3 (not_3_out, s[2]);
  Multiplexer #(.select(3), .enable("false")) multiplexer_1 (
    .in0(1'b0), .in1(or_1_out), .in2(xor_1_out), .in3(s[2]), .in4(not_3_out), .in5(not_1_out),
    .in6(not_2_out), .out(out_3), .sel(ifun[2:0]));  // open: in7

  // Notes on the sheet:
  //   0F
  //   SF
  //   ZF
endmodule

module setCC (
  input  [3:0] icode,
  output out_2
);

  and and_1 (out_2, ~icode[3], icode[2], icode[1], ~icode[0]);  // AND_Gate
endmodule

module dstE (
  input  [3:0] rB,
  input  Cnd,
  input  [3:0] icode,
  output [3:0] dstE
);

  wire and_1_out, and_2_out, and_3_out, and_4_out, not_1_out, not_2_out, not_3_out, not_4_out, not_5_out,
       not_6_out;
  wire [1:0] or_2_out;
  wire [3:0] multiplexer_1_out;

  not not_1 (not_1_out, icode[1]);
  and and_1 (and_1_out, icode[2], icode[0]);
  not not_2 (not_2_out, icode[3]);
  not not_3 (not_3_out, icode[2]);
  not not_4 (not_4_out, icode[0]);
  not not_5 (not_5_out, icode[3]);
  not not_6 (not_6_out, icode[1]);
  or or_1 (or_2_out[1], not_1_out, and_1_out, icode[3]);
  and and_2 (and_2_out, not_2_out, not_3_out, not_4_out);
  and and_3 (and_3_out, not_5_out, not_6_out);
  or or_2 (or_2_out[0], and_2_out, and_3_out, and_4_out);
  and and_4 (and_4_out, icode[2], icode[0]);
  Multiplexer #(.width(4), .enable("false")) multiplexer_1 (
    .in0(4'b1111), .in1(rB), .out(multiplexer_1_out), .sel(Cnd));
  Multiplexer #(.select(2), .width(4), .enable("false")) multiplexer_2 (
    .in0(rB), .in1(multiplexer_1_out), .in2(4'b0100), .in3(4'b1111), .out(dstE), .sel(or_2_out));
endmodule

module dstM (
  input  [3:0] rA,
  input  [3:0] icode,
  output [3:0] dstM
);

  wire and_1_out, and_2_out, and_3_out, not_1_out, not_2_out, not_3_out, not_4_out, not_5_out, not_6_out,
       or_1_out;

  not not_1 (not_1_out, icode[3]);
  not not_2 (not_2_out, icode[2]);
  not not_3 (not_3_out, icode[2]);
  not not_4 (not_4_out, icode[1]);
  not not_5 (not_5_out, icode[3]);
  and and_1 (and_1_out, not_1_out, not_2_out);
  and and_2 (and_2_out, not_3_out, not_4_out);
  not not_6 (not_6_out, icode[0]);
  and and_3 (and_3_out, not_5_out, icode[1]);
  or or_1 (or_1_out, and_1_out, and_2_out, not_6_out, and_3_out);
  Multiplexer #(.width(4), .enable("false")) multiplexer_1 (.in0(rA), .in1(4'b1111), .out(dstM), .sel(or_1_out));
endmodule

module srcAB (
  input  [3:0] rA,
  input  [3:0] icode,
  input  [3:0] rB,
  output [3:0] srcA,
  output [3:0] srrcB
);

  wire and_1_out, and_2_out, and_3_out, and_4_out, and_5_out, not_1_out, not_2_out, not_3_out, not_4_out,
       not_5_out, not_6_out, not_7_out;
  wire [1:0] not_8_out;
  wire [1:1] or_1_out;

  not not_1 (not_1_out, icode[2]);
  not not_2 (not_2_out, icode[1]);
  not not_3 (not_3_out, icode[0]);
  not not_4 (not_4_out, icode[3]);
  not not_5 (not_5_out, icode[3]);
  not not_6 (not_6_out, icode[2]);
  not not_7 (not_7_out, icode[3]);
  not not_8 (not_8_out[0], icode[2]);
  and and_1 (and_1_out, not_1_out, not_2_out, not_3_out);
  or or_1 (or_1_out[1], and_1_out, and_2_out, and_3_out);
  and and_2 (and_2_out, not_4_out, icode[0]);
  and and_3 (and_3_out, icode[3], icode[2]);
  and and_4 (and_4_out, not_5_out, not_6_out);
  or or_2 (not_8_out[1], and_4_out, and_5_out);
  and and_5 (and_5_out, not_7_out, icode[1], icode[0]);
  Multiplexer #(.select(2), .width(4), .enable("false")) multiplexer_1 (
    .in0(rA), .in1(4'b0100), .in2(4'b1111), .in3(4'b0000), .out(srcA), .sel({or_1_out[1], icode[0]}));
  Multiplexer #(.select(2), .width(4), .enable("false")) multiplexer_2 (
    .in0(rB), .in1(4'b0100), .in2(4'b1111), .in3(4'b0000), .out(srrcB), .sel(not_8_out));
endmodule

module Split (
  input  imemerr,
  input  [7:0] B0,
  output valid,
  output [3:0] ifun,
  output [3:0] icode
);

  wire not_1_out, or_1_out;

  not not_1 (not_1_out, B0[2]);
  or or_1 (or_1_out, not_1_out, B0[3], B0[1], B0[0]);
  and and_1 (valid, imemerr, or_1_out);

  assign icode = B0[7:4];
  assign ifun = B0[3:0];
endmodule

module needreg (
  input  [3:0] icode,
  output needreg
);

  wire and_1_out, and_2_out, and_3_out, not_1_out, not_2_out, not_3_out;

  not not_1 (not_1_out, icode[2]);
  not not_2 (not_2_out, icode[0]);
  not not_3 (not_3_out, icode[1]);
  and and_1 (and_1_out, not_1_out, icode[1]);
  or or_1 (needreg, and_1_out, and_2_out, and_3_out);
  and and_2 (and_2_out, icode[1], not_2_out);
  and and_3 (and_3_out, icode[2], not_3_out);
endmodule

module needvalC (
  input  [3:0] icode,
  output needvalc
);

  wire and_1_out, and_2_out, and_3_out, not_1_out, not_2_out, not_3_out, not_4_out;

  not not_1 (not_1_out, icode[3]);
  not not_2 (not_2_out, icode[1]);
  not not_3 (not_3_out, icode[1]);
  not not_4 (not_4_out, icode[0]);
  and and_1 (and_1_out, not_1_out, icode[1], icode[0]);
  and and_2 (and_2_out, icode[2], not_2_out);
  and and_3 (and_3_out, icode[3], not_3_out, not_4_out);
  or or_1 (needvalc, and_1_out, and_2_out, and_3_out);
endmodule

// PCinc
module PCincrement (
  input  needReg,
  input  [31:0] pcin_32,
  input  needvalC,
  output [31:0] valP
);

  wire adder_1_cout, adder_2_cout;
  wire [31:0] adder_1_out, adder_2_out, multiplexer_1_out, multiplexer_2_out;

  Multiplexer #(.width(32), .enable("false")) multiplexer_1 (
    .in0({32{1'b0}}), .in1(32'h1), .out(multiplexer_1_out), .sel(needReg));
  Multiplexer #(.width(32), .enable("false")) multiplexer_2 (
    .in0({32{1'b0}}), .in1(32'h8), .out(multiplexer_2_out), .sel(needvalC));
  Adder #(.width(32)) adder_1 (.a(32'h1), .b(multiplexer_1_out), .out(adder_1_out), .cin(1'b0), .cout(adder_1_cout));
  Adder #(.width(32)) adder_2 (
    .a(adder_1_out), .b(multiplexer_2_out), .out(adder_2_out), .cin(adder_1_cout), .cout(adder_2_cout));
  Adder #(.width(32)) adder_3 (.a(adder_2_out), .b(pcin_32), .out(valP), .cin(adder_2_cout));  // open: cout
endmodule

module stat (
  input  [3:0] icode,
  input  instr_valid,
  input  imem_err,
  input  dmem_err,
  output [1:0] out_5
);

  wire and_1_out, and_2_out, and_3_out, not_1_out, not_2_out, or_1_out;

  and and_1 (and_1_out, ~icode[0], ~icode[1], ~icode[2], ~icode[3]);  // AND_Gate
  not not_1 (not_1_out, instr_valid);
  not not_2 (not_2_out, instr_valid);
  and and_2 (and_2_out, not_1_out, dmem_err);
  and and_3 (and_3_out, not_2_out, imem_err);
  or or_1 (or_1_out, and_2_out, and_3_out);
  or or_2 (out_5[0], and_1_out, or_1_out);
  or or_3 (out_5[1], and_1_out, instr_valid);
endmodule

module should_have_listened_to_gabby (
  input  i3,
  input  i2,
  input  i1,
  input  i0,
  output s0
);

  wire and_1_out, and_2_out, and_3_out, not_1_out, not_2_out, not_3_out, not_4_out;

  not not_1 (not_1_out, i3);
  and and_1 (and_1_out, not_1_out, i1, i0);
  and and_2 (and_2_out, i2, not_2_out);
  not not_2 (not_2_out, i1);
  not not_3 (not_3_out, i1);
  and and_3 (and_3_out, i3, not_3_out, not_4_out);
  not not_4 (not_4_out, i0);
  or or_1 (s0, and_1_out, and_2_out, and_3_out);
endmodule
